// Logisim project memory-controller.circ as structural Verilog: 1 circuit, main circuit memory_controller
module memory_controller (
  input  write_enable,
  input  clock,
  input  byte__0__or_word__1,
  input  [15:0] write_data,
  input  [31:0] mem_D_out,
  input  [15:0] address,
  output mem_str,
  output mem_sel,
  output mem_clk,
  output mem_ld,
  output mem_clr,
  output [13:0] mem_A,
  output [15:0] data_out,
  output [31:0] mem_D_in
);

  wire [7:0] multiplexer_5_out;
  wire [15:0] bit_extender_1_out, multiplexer_4_out;
  wire [31:0] multiplexer_2_out, multiplexer_3_out;

  Multiplexer #(.width(32), .enable("false")) multiplexer_1 (
    .in0(multiplexer_2_out), .in1(multiplexer_3_out), .out(mem_D_in), .sel(byte__0__or_word__1));
  Multiplexer #(.select(2), .width(32), .enable("false")) multiplexer_2 (
    .in0({mem_D_out[31:8], write_data[7:0]}), .in1({mem_D_out[31:16], write_data[7:0], mem_D_out[7:0]}),
    .in2({mem_D_out[31:24], write_data[7:0], mem_D_out[15:0]}), .in3({write_data[7:0], mem_D_out[23:0]}),
    .out(multiplexer_2_out), .sel(address[1:0]));
  Multiplexer #(.width(32), .enable("false")) multiplexer_3 (
    .in0({mem_D_out[31:16], write_data}), .in1({write_data, mem_D_out[15:0]}), .out(multiplexer_3_out),
    .sel(address[1]));
  Multiplexer #(.width(16), .enable("false")) multiplexer_4 (
    .in0(mem_D_out[15:0]), .in1(mem_D_out[31:16]), .out(multiplexer_4_out), .sel(address[1]));
  Multiplexer #(.select(2), .width(8), .enable("false")) multiplexer_5 (
    .in0(mem_D_out[7:0]), .in1(mem_D_out[15:8]), .in2(mem_D_out[23:16]), .in3(mem_D_out[31:24]),
    .out(multiplexer_5_out), .sel(address[1:0]));
  assign bit_extender_1_out = {{8{1'b0}}, multiplexer_5_out};  // Bit_Extender bit_extender_1
  Multiplexer #(.width(16), .enable("false")) multiplexer_6 (
    .in0(bit_extender_1_out), .in1(multiplexer_4_out), .out(data_out), .sel(byte__0__or_word__1));

  assign mem_A = address[15:2];
  assign mem_clk = clock;
  assign mem_clr = 1'b0;
  assign mem_ld = 1'b1;
  assign mem_sel = 1'b1;
  assign mem_str = write_enable;
endmodule
